# Fritzing sketch SimpleStepTracking (saved by Fritzing 0.9.3b)
breadboards: 1

parts:
  Part1 = Adafruit Feather nRF52 [part_number="Adafruit #3406"]
  J1 = Basic Force Sensing Resistor (FSR) [package=THT]
  Part3 = InvenSense MPU6050
  Part2 = Adafruit Adalogger FeatherWing [part_number="Adafruit #2922"]  # not connected
  R2 = Resistor [tolerance=±5% resistance=4.7k package="2512 [SMD]"]
  R3 = Resistor [tolerance=±5% resistance=4.7k package="2512 [SMD]"]
  R1 = Resistor [tolerance=±5% resistance=220 package=THT]

nets:
  3.3V: Part1.3.3V, J1.pin_1, Part3.VCC, Part3.AD0, R2.Pin_0, R3.Pin_0, R1.Pin_0
  GND: Part1.GND, Part3.GND
  N1: Part1.A1/0.03, J1.pin_0, R1.Pin_1
  N2: Part1.SDA, Part3.SDA, R3.Pin_1
  N3: Part1.SCL, Part3.SCL, R2.Pin_1

custom parts:
  Adafruit Adalogger FeatherWing: This is the Adalogger FeatherWing: it adds both a battery-backed Real Time Clock and micro SD card storage to any Feather main board. This FeatherWing will make it real easy to add datalogging to any of our existing Feathers. You get both an I2C real time clock (PCF8523) with 32KHz crystal and battery backup, and a microSD socket that connects to the SPI port pins (+ extra pin for CS). Tested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
